// Logisim project ALUandShiftingOperations.circ as structural Verilog: 1 circuit, main circuit main
module main (
  input  [3:0] S3S2S1S0,
  input  [7:0] X,
  input  [7:0] Y,
  output N,
  output C,
  output V,
  output [7:0] G,
  output Z
);

  wire and_2_out, and_3_out, and_4_out;
  wire [6:0] adder_1_out;
  wire [7:0] and_1_out, multiplexer_1_out, multiplexer_2_out, multiplexer_3_out, multiplexer_4_out,
       nor_1_out, not_1_out, not_2_out, xor_1_out;

  assign not_1_out = ~Y;  // NOT_Gate not_1, 8 bits wide
  Multiplexer #(.select(3), .width(8)) multiplexer_1 (
    .in0(8'h3), .in1(8'h3), .in2(not_1_out), .in3(not_1_out), .in4({8{1'b0}}), .in5({8{1'b0}}), .in6(Y),
    .in7(Y), .out(multiplexer_1_out), .sel(S3S2S1S0[2:0]));  // open: en
  assign and_1_out = X & Y;  // AND_Gate and_1, 8 bits wide
  assign not_2_out = ~X;  // NOT_Gate not_2, 8 bits wide
  assign nor_1_out = ~(X | Y);  // NOR_Gate nor_1, 8 bits wide
  assign xor_1_out = X ^ Y;  // XOR_Gate xor_1, 8 bits wide
  Multiplexer #(.select(2), .width(8)) multiplexer_2 (
    .in0(and_1_out), .in1(not_2_out), .in2(nor_1_out), .in3(xor_1_out), .out(multiplexer_2_out),
    .sel(S3S2S1S0[1:0]));  // open: en
  Adder adder_1 (.a(X), .b(multiplexer_1_out), .out({N, adder_1_out}), .cin(S3S2S1S0[0]), .cout(C));
  Multiplexer #(.select(2), .width(8)) multiplexer_3 (
    .in0(Y), .in1({Y[6:0], Y[7]}), .in2({1'b0, Y[7:1]}), .in3({{2{Y[7]}}, Y[6:1]}), .out(multiplexer_3_out),
    .sel(S3S2S1S0[1:0]));  // open: en
  Multiplexer #(.width(8)) multiplexer_4 (
    .in0({N, adder_1_out}), .in1(multiplexer_2_out), .out(multiplexer_4_out), .sel(S3S2S1S0[3]));  // open: en
  and and_2 (and_2_out, S3S2S1S0[3], S3S2S1S0[2]);
  Multiplexer #(.width(8)) multiplexer_5 (
    .in0(multiplexer_4_out), .in1(multiplexer_3_out), .out(G), .sel(and_2_out));  // open: en
  and and_3 (and_3_out, ~X[7], N, ~multiplexer_1_out[7]);  // AND_Gate
  and and_4 (and_4_out, X[7], ~N, multiplexer_1_out[7]);  // AND_Gate
  or or_1 (V, and_3_out, and_4_out);
  nor nor_2 (Z, G[0], G[1], G[2], G[3], G[4], G[5], G[6], G[7]);
endmodule
